// Logisim project Ejercicio1.circ as structural Verilog: 9 circuits, main circuit Ejercicio 1
module Ejercicio_1 (
  input  A,
  input  B,
  input  Acarreo0,
  input  [1:0] _10___Suma,
  output Salida,
  output Acarreo1
);

  wire and_1_out, or_1_out, sumador_1_s;

  and and_1 (and_1_out, A, B);
  or or_1 (or_1_out, A, B);
  Sumador sumador_1 (.Ci(Acarreo0), .B(B), .A(A), .Co(Acarreo1), .S(sumador_1_s));
  Multiplexer #(.select(2)) multiplexer_1 (
    .in0(and_1_out), .in1(or_1_out), .in2(sumador_1_s), .out(Salida), .sel(_10___Suma));  // open: in3, en

  // Notes on the sheet:
  //   00 - AND
  //   01 - OR
endmodule

module Ejercicio_2 (
  input  A,
  input  in_2,
  input  in_3,
  input  in_4,
  input  in_5,
  input  in_6,
  input  in_7,
  input  in_8,
  input  B,
  input  in_10,
  input  in_11,
  input  in_12,
  input  in_13,
  input  in_14,
  input  in_15,
  input  in_16,
  input  Acarreo,
  input  [1:0] in_18,
  output out_19,
  output out_20,
  output out_21,
  output out_22,
  output out_23,
  output out_24,
  output out_25,
  output out_26,
  output out_27
);

  wire ejercicio_1_1_acarreo1, ejercicio_1_2_acarreo1, ejercicio_1_3_acarreo1, ejercicio_1_4_acarreo1,
       ejercicio_1_5_acarreo1, ejercicio_1_6_acarreo1, ejercicio_1_7_acarreo1;

  Ejercicio_1 ejercicio_1_1 (
    .A(A), .B(B), .Acarreo0(Acarreo), ._10___Suma(in_18), .Salida(out_19), .Acarreo1(ejercicio_1_1_acarreo1));
  Ejercicio_1 ejercicio_1_2 (
    .A(in_2), .B(in_10), .Acarreo0(ejercicio_1_1_acarreo1), ._10___Suma(in_18), .Salida(out_20),
    .Acarreo1(ejercicio_1_2_acarreo1));
  Ejercicio_1 ejercicio_1_3 (
    .A(in_3), .B(in_11), .Acarreo0(ejercicio_1_2_acarreo1), ._10___Suma(in_18), .Salida(out_21),
    .Acarreo1(ejercicio_1_3_acarreo1));
  Ejercicio_1 ejercicio_1_4 (
    .A(in_4), .B(in_12), .Acarreo0(ejercicio_1_3_acarreo1), ._10___Suma(in_18), .Salida(out_22),
    .Acarreo1(ejercicio_1_4_acarreo1));
  Ejercicio_1 ejercicio_1_5 (
    .A(in_5), .B(in_13), .Acarreo0(ejercicio_1_4_acarreo1), ._10___Suma(in_18), .Salida(out_23),
    .Acarreo1(ejercicio_1_5_acarreo1));
  Ejercicio_1 ejercicio_1_6 (
    .A(in_6), .B(in_14), .Acarreo0(ejercicio_1_5_acarreo1), ._10___Suma(in_18), .Salida(out_24),
    .Acarreo1(ejercicio_1_6_acarreo1));
  Ejercicio_1 ejercicio_1_7 (
    .A(in_7), .B(in_15), .Acarreo0(ejercicio_1_6_acarreo1), ._10___Suma(in_18), .Salida(out_25),
    .Acarreo1(ejercicio_1_7_acarreo1));
  Ejercicio_1 ejercicio_1_8 (
    .A(in_8), .B(in_16), .Acarreo0(ejercicio_1_7_acarreo1), ._10___Suma(in_18), .Salida(out_26),
    .Acarreo1(out_27));

  // Notes on the sheet:
  //   Resultado de suma
  //   Ingresar en 10 para realizar suma
endmodule

module Ejercicio_3 (
  input  in_1,
  input  A,
  input  B,
  input  in_4,
  input  [1:0] in_5,
  input  in_6,
  output out_7,
  output Resultado,
  output out_9
);

  wire ejercicio_1_1_salida, restador_1_s;

  Ejercicio_1 ejercicio_1_1 (
    .A(A), .B(B), .Acarreo0(in_4), ._10___Suma(in_5), .Salida(ejercicio_1_1_salida), .Acarreo1(out_9));
  Restador restador_1 (.B(A), .A(B), .Ci(in_1), .C0(out_7), .S(restador_1_s));
  Multiplexer multiplexer_1 (.in0(restador_1_s), .in1(ejercicio_1_1_salida), .out(Resultado), .sel(in_6));  // open: en

  // Notes on the sheet:
  //   Mantener en 10 para suma
  //   Acarreo de resta
  //   Acarreo de suma
  //   0 - Resta           1 - suma
endmodule

module Ejercico_4 (
  input  A,
  input  in_2,
  input  in_3,
  input  in_4,
  input  in_5,
  input  in_6,
  input  in_7,
  input  in_8,
  input  B,
  input  in_10,
  input  in_11,
  input  in_12,
  input  in_13,
  input  in_14,
  input  in_15,
  input  in_16,
  input  in_17,
  input  in_18,
  input  _0___Resta,
  input  [1:0] in_20,
  output out_21,
  output out_22,
  output out_23,
  output out_24,
  output out_25,
  output out_26,
  output out_27,
  output out_28,
  output out_29,
  output out_30,
  output out_31
);

  wire ejercicio_3_1_out_7, ejercicio_3_1_out_9, ejercicio_3_2_out_7, ejercicio_3_2_out_9,
       ejercicio_3_3_out_7, ejercicio_3_3_out_9, ejercicio_3_4_out_7, ejercicio_3_4_out_9,
       ejercicio_3_5_out_7, ejercicio_3_5_out_9, ejercicio_3_6_out_7, ejercicio_3_6_out_9,
       ejercicio_3_7_out_7, ejercicio_3_7_out_9, not_1_out, not_2_out, not_3_out, not_4_out, not_5_out,
       not_6_out, not_7_out, not_8_out, not_9_out;

  Ejercicio_3 ejercicio_3_1 (
    .in_1(in_17), .A(A), .B(B), .in_4(in_18), .in_5(in_20), .out_7(ejercicio_3_1_out_7), .Resultado(out_22),
    .out_9(ejercicio_3_1_out_9), .in_6(_0___Resta));
  not not_1 (not_1_out, out_22);
  Ejercicio_3 ejercicio_3_2 (
    .in_1(ejercicio_3_1_out_7), .A(in_2), .B(in_10), .in_4(ejercicio_3_1_out_9), .in_5(in_20),
    .out_7(ejercicio_3_2_out_7), .Resultado(out_23), .out_9(ejercicio_3_2_out_9), .in_6(_0___Resta));
  not not_2 (not_2_out, out_23);
  Ejercicio_3 ejercicio_3_3 (
    .in_1(ejercicio_3_2_out_7), .A(in_3), .B(in_11), .in_4(ejercicio_3_2_out_9), .in_5(in_20),
    .out_7(ejercicio_3_3_out_7), .Resultado(out_24), .out_9(ejercicio_3_3_out_9), .in_6(_0___Resta));
  not not_3 (not_3_out, out_24);
  Ejercicio_3 ejercicio_3_4 (
    .in_1(ejercicio_3_3_out_7), .A(in_4), .B(in_12), .in_4(ejercicio_3_3_out_9), .in_5(in_20),
    .out_7(ejercicio_3_4_out_7), .Resultado(out_25), .out_9(ejercicio_3_4_out_9), .in_6(_0___Resta));
  not not_4 (not_4_out, out_25);
  Ejercicio_3 ejercicio_3_5 (
    .in_1(ejercicio_3_4_out_7), .A(in_5), .B(in_13), .in_4(ejercicio_3_4_out_9), .in_5(in_20),
    .out_7(ejercicio_3_5_out_7), .Resultado(out_26), .out_9(ejercicio_3_5_out_9), .in_6(_0___Resta));
  and and_1 (out_31, not_1_out, not_2_out, not_3_out, not_4_out, not_5_out, not_6_out, not_7_out, not_8_out, not_9_out);
  not not_5 (not_5_out, out_26);
  Ejercicio_3 ejercicio_3_6 (
    .in_1(ejercicio_3_5_out_7), .A(in_6), .B(in_14), .in_4(ejercicio_3_5_out_9), .in_5(in_20),
    .out_7(ejercicio_3_6_out_7), .Resultado(out_27), .out_9(ejercicio_3_6_out_9), .in_6(_0___Resta));
  not not_6 (not_6_out, out_27);
  Ejercicio_3 ejercicio_3_7 (
    .in_1(ejercicio_3_6_out_7), .A(in_7), .B(in_15), .in_4(ejercicio_3_6_out_9), .in_5(in_20),
    .out_7(ejercicio_3_7_out_7), .Resultado(out_28), .out_9(ejercicio_3_7_out_9), .in_6(_0___Resta));
  not not_7 (not_7_out, out_28);
  Ejercicio_3 ejercicio_3_8 (
    .in_1(ejercicio_3_7_out_7), .A(in_8), .B(in_16), .in_4(ejercicio_3_7_out_9), .in_5(in_20),
    .out_7(out_29), .Resultado(out_29), .out_9(out_21), .in_6(_0___Resta));
  not not_8 (not_8_out, out_29);
  not not_9 (not_9_out, out_29);

  assign out_30 = out_29;

  // Notes on the sheet:
  //   0 Si los números son diferentes
  //   1 si los números son iguales
endmodule

module Sumador (
  input  B,
  input  A,
  input  Ci,
  output S,
  output Co
);

  wire and_1_out, and_2_out, xor_1_out;

  and and_1 (and_1_out, B, A);
  xor xor_1 (xor_1_out, B, A);
  xor xor_2 (S, xor_1_out, Ci);
  and and_2 (and_2_out, xor_1_out, Ci);
  or or_1 (Co, and_2_out, and_1_out);
endmodule

module Restador (
  input  Ci,
  input  B,
  input  A,
  output S,
  output C0
);

  wire and_1_out, and_2_out, and_3_out, not_1_out, xor_1_out;

  not not_1 (not_1_out, B);
  xor xor_1 (xor_1_out, B, A);
  and and_1 (and_1_out, not_1_out, A);
  and and_2 (and_2_out, Ci, not_1_out);
  and and_3 (and_3_out, Ci, A);
  xor xor_2 (S, Ci, xor_1_out);
  or or_1 (C0, and_1_out, and_2_out, and_3_out);
endmodule

module ALU_con_NOR (
  input  A,
  input  B,
  input  Acarreo0,
  input  [1:0] _11__NOR,
  output Salida,
  output Acarreo1
);

  wire and_1_out, not_1_out, or_1_out, sumador_1_s;

  and and_1 (and_1_out, A, B);
  or or_1 (or_1_out, A, B);
  Sumador sumador_1 (.Ci(Acarreo0), .B(B), .A(A), .Co(Acarreo1), .S(sumador_1_s));
  not not_1 (not_1_out, or_1_out);
  Multiplexer #(.select(2)) multiplexer_1 (
    .in0(and_1_out), .in1(or_1_out), .in2(sumador_1_s), .in3(not_1_out), .out(Salida), .sel(_11__NOR));  // open: en

  // Notes on the sheet:
  //   00 - AND
  //   01 - OR
  //   10 - Suma
endmodule

module Ejercicio_5 (
  input  in_1,
  input  A,
  input  B,
  input  in_4,
  input  [1:0] in_5,
  input  in_6,
  output out_7,
  output Resultado,
  output out_9
);

  wire alu_con_nor_1_salida, restador_1_s;

  ALU_con_NOR alu_con_nor_1 (
    .A(A), .B(B), .Acarreo0(in_4), ._11__NOR(in_5), .Salida(alu_con_nor_1_salida), .Acarreo1(out_9));
  Restador restador_1 (.B(A), .A(B), .Ci(in_1), .C0(out_7), .S(restador_1_s));
  Multiplexer multiplexer_1 (.in0(restador_1_s), .in1(alu_con_nor_1_salida), .out(Resultado), .sel(in_6));  // open: en

  // Notes on the sheet:
  //   Mantener en 10 para suma
  //   Acarreo de resta
  //   Acarreo de suma
  //   0 - Resta           1 - suma
endmodule

module Ejercicio_6 (
  input  A,
  input  in_2,
  input  in_3,
  input  in_4,
  input  in_5,
  input  in_6,
  input  in_7,
  input  in_8,
  input  B,
  input  in_10,
  input  in_11,
  input  in_12,
  input  in_13,
  input  in_14,
  input  in_15,
  input  in_16,
  input  in_17,
  input  in_18,
  input  in_19,
  input  [1:0] in_20,
  output out_21,
  output out_22,
  output out_23,
  output out_24,
  output out_25,
  output out_26,
  output out_27,
  output out_28,
  output out_29,
  output out_30,
  output out_31
);

  wire ejercicio_5_1_out_7, ejercicio_5_1_out_9, ejercicio_5_2_out_7, ejercicio_5_2_out_9,
       ejercicio_5_3_out_7, ejercicio_5_3_out_9, ejercicio_5_4_out_7, ejercicio_5_4_out_9,
       ejercicio_5_5_out_7, ejercicio_5_5_out_9, ejercicio_5_6_out_7, ejercicio_5_6_out_9,
       ejercicio_5_7_out_7, ejercicio_5_7_out_9, not_1_out, not_2_out, not_3_out, not_4_out, not_5_out,
       not_6_out, not_7_out, not_8_out, not_9_out;

  Ejercicio_5 ejercicio_5_1 (
    .in_1(in_17), .A(A), .B(B), .in_4(in_18), .in_5(in_20), .out_7(ejercicio_5_1_out_7), .Resultado(out_22),
    .out_9(ejercicio_5_1_out_9), .in_6(in_19));
  not not_1 (not_1_out, out_22);
  Ejercicio_5 ejercicio_5_2 (
    .in_1(ejercicio_5_1_out_7), .A(in_2), .B(in_10), .in_4(ejercicio_5_1_out_9), .in_5(in_20),
    .out_7(ejercicio_5_2_out_7), .Resultado(out_23), .out_9(ejercicio_5_2_out_9), .in_6(in_19));
  not not_2 (not_2_out, out_23);
  Ejercicio_5 ejercicio_5_3 (
    .in_1(ejercicio_5_2_out_7), .A(in_3), .B(in_11), .in_4(ejercicio_5_2_out_9), .in_5(in_20),
    .out_7(ejercicio_5_3_out_7), .Resultado(out_24), .out_9(ejercicio_5_3_out_9), .in_6(in_19));
  not not_3 (not_3_out, out_24);
  Ejercicio_5 ejercicio_5_4 (
    .in_1(ejercicio_5_3_out_7), .A(in_4), .B(in_12), .in_4(ejercicio_5_3_out_9), .in_5(in_20),
    .out_7(ejercicio_5_4_out_7), .Resultado(out_25), .out_9(ejercicio_5_4_out_9), .in_6(in_19));
  not not_4 (not_4_out, out_25);
  Ejercicio_5 ejercicio_5_5 (
    .in_1(ejercicio_5_4_out_7), .A(in_5), .B(in_13), .in_4(ejercicio_5_4_out_9), .in_5(in_20),
    .out_7(ejercicio_5_5_out_7), .Resultado(out_26), .out_9(ejercicio_5_5_out_9), .in_6(in_19));
  and and_1 (out_31, not_1_out, not_2_out, not_3_out, not_4_out, not_5_out, not_6_out, not_7_out, not_8_out, not_9_out);
  not not_5 (not_5_out, out_26);
  Ejercicio_5 ejercicio_5_6 (
    .in_1(ejercicio_5_5_out_7), .A(in_6), .B(in_14), .in_4(ejercicio_5_5_out_9), .in_5(in_20),
    .out_7(ejercicio_5_6_out_7), .Resultado(out_27), .out_9(ejercicio_5_6_out_9), .in_6(in_19));
  not not_6 (not_6_out, out_27);
  Ejercicio_5 ejercicio_5_7 (
    .in_1(ejercicio_5_6_out_7), .A(in_7), .B(in_15), .in_4(ejercicio_5_6_out_9), .in_5(in_20),
    .out_7(ejercicio_5_7_out_7), .Resultado(out_28), .out_9(ejercicio_5_7_out_9), .in_6(in_19));
  not not_7 (not_7_out, out_28);
  Ejercicio_5 ejercicio_5_8 (
    .in_1(ejercicio_5_7_out_7), .A(in_8), .B(in_16), .in_4(ejercicio_5_7_out_9), .in_5(in_20),
    .out_7(out_30), .Resultado(out_29), .out_9(out_21), .in_6(in_19));
  not not_8 (not_8_out, out_29);
  not not_9 (not_9_out, out_30);

  // Notes on the sheet:
  //   0 Si los números son diferentes
  //   1 si los números son iguales
endmodule
