// Logisim project Ejercicio2.circ as structural Verilog: 6 circuits, main circuit Ejercicio 1
module Ejercicio_1 (
);

  wire and_1_out, and_2_out, and_3_out, bcd_1_a_2, bcd_1_b_2, bcd_1_c_2, bcd_1_d_2, bcd_1_e, bcd_1_f,
       bcd_1_g, clock_1_out, j_k_ff_1_q, j_k_ff_1_qn, j_k_ff_2_q, j_k_ff_2_qn, j_k_ff_3_q, j_k_ff_3_qn,
       j_k_ff_4_q, j_k_ff_4_qn;

  Clock clock_1 (.out(clock_1_out));
  J_K_Flip_Flop j_k_ff_1 (
    .J(1'b1), .clk(clock_1_out), .K(1'b1), .Q(j_k_ff_1_q), .Qn(j_k_ff_1_qn));  // open: preset, en, reset
  and and_1 (and_1_out, j_k_ff_4_qn, j_k_ff_1_q);
  J_K_Flip_Flop j_k_ff_2 (
    .J(and_1_out), .clk(clock_1_out), .K(j_k_ff_1_q), .Q(j_k_ff_2_q), .Qn(j_k_ff_2_qn));  // open: preset, en, reset
  and and_2 (and_2_out, j_k_ff_1_q, j_k_ff_2_q);
  BCD bcd_1 (
    .D(j_k_ff_4_q), .C(j_k_ff_3_q), .B(j_k_ff_2_q), .A(j_k_ff_1_q), .a_2(bcd_1_a_2), .b_2(bcd_1_b_2),
    .c_2(bcd_1_c_2), .d_2(bcd_1_d_2), .e(bcd_1_e), .f(bcd_1_f), .g(bcd_1_g));
  J_K_Flip_Flop j_k_ff_3 (
    .J(and_2_out), .clk(clock_1_out), .K(and_2_out), .Q(j_k_ff_3_q), .Qn(j_k_ff_3_qn));  // open: preset, en, reset
  and and_3 (and_3_out, and_2_out, j_k_ff_3_q);
  _7_Segment_Display u_7_segment_display_1 (
    .g(bcd_1_g), .f(bcd_1_f), .a(bcd_1_a_2), .b(bcd_1_b_2), .e(bcd_1_e), .d(bcd_1_d_2), .c(bcd_1_c_2));  // open: dp
  J_K_Flip_Flop j_k_ff_4 (
    .J(and_3_out), .clk(clock_1_out), .K(j_k_ff_1_q), .Q(j_k_ff_4_q), .Qn(j_k_ff_4_qn));  // open: preset, en, reset
endmodule

module BCD (
  input  D,
  input  C,
  input  B,
  input  A,
  output a_2,
  output b_2,
  output c_2,
  output d_2,
  output e,
  output f,
  output g
);

  wire and_1_out, and_2_out, and_3_out, and_4_out, and_5_out, and_6_out, and_7_out, and_8_out, and_9_out,
       and_10_out, and_11_out, and_12_out, and_13_out, and_14_out, and_15_out, and_16_out, and_17_out,
       and_18_out, and_19_out, and_20_out, and_21_out, and_22_out, and_23_out, and_24_out, not_1_out,
       not_2_out, not_3_out, not_4_out, not_5_out, not_6_out, not_7_out, not_8_out, not_9_out, not_10_out,
       not_11_out, not_12_out, not_13_out, not_14_out, not_15_out, not_16_out, not_17_out, not_18_out,
       not_19_out, not_20_out, not_21_out, not_22_out, not_23_out, not_24_out, not_25_out, not_26_out,
       not_27_out, not_28_out, not_29_out;

  not not_1 (not_1_out, C);
  and and_1 (and_1_out, not_1_out, not_2_out);
  not not_2 (not_2_out, A);
  and and_2 (and_2_out, C, A);
  not not_3 (not_3_out, D);
  and and_3 (and_3_out, not_3_out, not_4_out);
  not not_4 (not_4_out, C);
  not not_5 (not_5_out, D);
  not not_6 (not_6_out, B);
  and and_4 (and_4_out, not_5_out, not_6_out, not_7_out);
  not not_7 (not_7_out, A);
  not not_8 (not_8_out, C);
  and and_5 (and_5_out, not_8_out, not_9_out);
  not not_9 (not_9_out, B);
  not not_10 (not_10_out, D);
  and and_6 (and_6_out, not_10_out, B, A);
  not not_11 (not_11_out, C);
  and and_7 (and_7_out, not_11_out, not_12_out);
  not not_12 (not_12_out, B);
  not not_13 (not_13_out, D);
  and and_8 (and_8_out, not_13_out, A);
  not not_14 (not_14_out, D);
  and and_9 (and_9_out, not_14_out, C);
  not not_15 (not_15_out, C);
  and and_10 (and_10_out, not_15_out, not_16_out);
  not not_16 (not_16_out, A);
  not not_17 (not_17_out, C);
  and and_11 (and_11_out, not_17_out, B);
  and and_12 (and_12_out, B, not_18_out);
  not not_18 (not_18_out, A);
  not not_19 (not_19_out, B);
  and and_13 (and_13_out, C, not_19_out, A);
  and and_14 (and_14_out, D, C);
  not not_20 (not_20_out, C);
  and and_15 (and_15_out, not_20_out, not_21_out);
  not not_21 (not_21_out, A);
  and and_16 (and_16_out, B, not_22_out);
  not not_22 (not_22_out, A);
  and and_17 (and_17_out, D, B);
  and and_18 (and_18_out, D, C);
  not not_23 (not_23_out, B);
  and and_19 (and_19_out, not_23_out, not_24_out);
  not not_24 (not_24_out, A);
  and and_20 (and_20_out, C, not_25_out);
  not not_25 (not_25_out, B);
  and and_21 (and_21_out, C, not_26_out);
  not not_26 (not_26_out, A);
  not not_27 (not_27_out, C);
  and and_22 (and_22_out, not_27_out, B);
  and and_23 (and_23_out, C, not_28_out);
  not not_28 (not_28_out, B);
  and and_24 (and_24_out, C, not_29_out);
  not not_29 (not_29_out, A);
  or or_1 (a_2, and_1_out, B, and_2_out, D);
  or or_2 (b_2, and_3_out, and_4_out, and_5_out, and_6_out);
  or or_3 (c_2, and_7_out, and_8_out, and_9_out);
  or or_4 (d_2, and_10_out, and_11_out, and_12_out, and_13_out, and_14_out);
  or or_5 (e, and_15_out, and_16_out, and_17_out, and_18_out);
  or or_6 (f, and_19_out, and_20_out, and_21_out, D);
  or or_7 (g, and_22_out, and_23_out, and_24_out, D);
endmodule

module Ejercicio_1_b (
);

  wire and_1_out, and_2_out, and_3_out, bcd_1_a_2, bcd_1_b_2, bcd_1_c_2, bcd_1_d_2, bcd_1_e, bcd_1_f,
       bcd_1_g, bcd_2_a_2, bcd_2_b_2, bcd_2_c_2, bcd_2_d_2, bcd_2_e, bcd_2_f, bcd_2_g, bcd_3_a_2, bcd_3_b_2,
       bcd_3_c_2, bcd_3_d_2, bcd_3_e, bcd_3_f, bcd_3_g, clock_1_out, j_k_ff_1_q, j_k_ff_1_qn, j_k_ff_2_q,
       j_k_ff_2_qn, j_k_ff_3_q, j_k_ff_3_qn, j_k_ff_4_q, j_k_ff_4_qn, j_k_ff_5_q, j_k_ff_5_qn, j_k_ff_6_q,
       j_k_ff_6_qn, j_k_ff_7_q, j_k_ff_7_qn, j_k_ff_8_q, j_k_ff_8_qn, j_k_ff_9_q, j_k_ff_9_qn, j_k_ff_10_q,
       j_k_ff_11_q, j_k_ff_12_q;

  Clock clock_1 (.out(clock_1_out));
  J_K_Flip_Flop j_k_ff_1 (
    .J(1'b1), .clk(and_2_out), .K(1'b1), .Q(j_k_ff_1_q), .Qn(j_k_ff_1_qn), .en(1'b1), .reset(and_3_out));  // open: preset
  J_K_Flip_Flop j_k_ff_2 (
    .J(1'b1), .clk(clock_1_out), .K(1'b1), .Q(j_k_ff_2_q), .Qn(j_k_ff_2_qn), .en(1'b1), .reset(and_1_out));  // open: preset
  J_K_Flip_Flop j_k_ff_3 (
    .J(1'b1), .clk(and_1_out), .K(1'b1), .Q(j_k_ff_3_q), .Qn(j_k_ff_3_qn), .en(1'b1), .reset(and_2_out));  // open: preset
  and and_1 (and_1_out, j_k_ff_10_q, j_k_ff_4_q);
  and and_2 (and_2_out, j_k_ff_11_q, j_k_ff_5_q);
  and and_3 (and_3_out, j_k_ff_12_q, j_k_ff_6_q);
  J_K_Flip_Flop j_k_ff_4 (
    .J(1'b1), .clk(j_k_ff_2_qn), .K(1'b1), .Q(j_k_ff_4_q), .Qn(j_k_ff_4_qn), .en(1'b1), .reset(and_1_out));  // open: preset
  J_K_Flip_Flop j_k_ff_5 (
    .J(1'b1), .clk(j_k_ff_3_qn), .K(1'b1), .Q(j_k_ff_5_q), .Qn(j_k_ff_5_qn), .en(1'b1), .reset(and_2_out));  // open: preset
  J_K_Flip_Flop j_k_ff_6 (
    .J(1'b1), .clk(j_k_ff_1_qn), .K(1'b1), .Q(j_k_ff_6_q), .Qn(j_k_ff_6_qn), .en(1'b1), .reset(and_3_out));  // open: preset
  J_K_Flip_Flop j_k_ff_7 (
    .J(1'b1), .clk(j_k_ff_4_qn), .K(1'b1), .Q(j_k_ff_7_q), .Qn(j_k_ff_7_qn), .en(1'b1), .reset(and_1_out));  // open: preset
  J_K_Flip_Flop j_k_ff_8 (
    .J(1'b1), .clk(j_k_ff_5_qn), .K(1'b1), .Q(j_k_ff_8_q), .Qn(j_k_ff_8_qn), .en(1'b1), .reset(and_2_out));  // open: preset
  J_K_Flip_Flop j_k_ff_9 (
    .J(1'b1), .clk(j_k_ff_6_qn), .K(1'b1), .Q(j_k_ff_9_q), .Qn(j_k_ff_9_qn), .en(1'b1), .reset(and_3_out));  // open: preset
  J_K_Flip_Flop j_k_ff_10 (
    .J(1'b1), .clk(j_k_ff_7_qn), .K(1'b1), .Q(j_k_ff_10_q), .en(1'b1), .reset(and_1_out));  // open: Qn, preset
  BCD bcd_1 (
    .D(j_k_ff_10_q), .C(j_k_ff_7_q), .B(j_k_ff_4_q), .A(j_k_ff_2_q), .a_2(bcd_1_a_2), .b_2(bcd_1_b_2),
    .c_2(bcd_1_c_2), .d_2(bcd_1_d_2), .e(bcd_1_e), .f(bcd_1_f), .g(bcd_1_g));
  J_K_Flip_Flop j_k_ff_11 (
    .J(1'b1), .clk(j_k_ff_8_qn), .K(1'b1), .Q(j_k_ff_11_q), .en(1'b1), .reset(and_2_out));  // open: Qn, preset
  BCD bcd_2 (
    .D(j_k_ff_11_q), .C(j_k_ff_8_q), .B(j_k_ff_5_q), .A(j_k_ff_3_q), .a_2(bcd_2_a_2), .b_2(bcd_2_b_2),
    .c_2(bcd_2_c_2), .d_2(bcd_2_d_2), .e(bcd_2_e), .f(bcd_2_f), .g(bcd_2_g));
  J_K_Flip_Flop j_k_ff_12 (
    .J(1'b1), .clk(j_k_ff_9_qn), .K(1'b1), .Q(j_k_ff_12_q), .en(1'b1), .reset(and_3_out));  // open: Qn, preset
  BCD bcd_3 (
    .D(j_k_ff_12_q), .C(j_k_ff_9_q), .B(j_k_ff_6_q), .A(j_k_ff_1_q), .a_2(bcd_3_a_2), .b_2(bcd_3_b_2),
    .c_2(bcd_3_c_2), .d_2(bcd_3_d_2), .e(bcd_3_e), .f(bcd_3_f), .g(bcd_3_g));
  _7_Segment_Display u_7_segment_display_1 (
    .g(bcd_1_g), .f(bcd_1_f), .a(bcd_1_a_2), .b(bcd_1_b_2), .e(bcd_1_e), .d(bcd_1_d_2), .c(bcd_1_c_2));  // open: dp
  _7_Segment_Display u_7_segment_display_2 (
    .g(bcd_2_g), .f(bcd_2_f), .a(bcd_2_a_2), .b(bcd_2_b_2), .e(bcd_2_e), .d(bcd_2_d_2), .c(bcd_2_c_2));  // open: dp
  _7_Segment_Display u_7_segment_display_3 (
    .g(bcd_3_g), .f(bcd_3_f), .a(bcd_3_a_2), .b(bcd_3_b_2), .e(bcd_3_e), .d(bcd_3_d_2), .c(bcd_3_c_2));  // open: dp
endmodule

module Ejercicio_2 (
  input  C
);

  wire and_1_out, and_2_out, and_3_out, and_4_out, clock_1_out, d_ff_1_q, d_ff_1_qn, d_ff_2_q, d_ff_2_qn,
       not_1_out, or_1_out, or_2_out;

  not not_1 (not_1_out, C);
  Clock clock_1 (.out(clock_1_out));
  and and_1 (and_1_out, not_1_out, d_ff_2_qn);
  D_Flip_Flop d_ff_1 (.clk(clock_1_out), .D(or_2_out), .Q(d_ff_1_q), .Qn(d_ff_1_qn));  // open: preset, en, reset
  D_Flip_Flop d_ff_2 (.clk(clock_1_out), .D(and_1_out), .Q(d_ff_2_q), .Qn(d_ff_2_qn));  // open: preset, en, reset
  and and_2 (and_2_out, C, d_ff_1_q);
  and and_3 (and_3_out, d_ff_2_q, not_1_out, d_ff_1_qn);
  and and_4 (and_4_out, d_ff_1_q, d_ff_2_qn);
  or or_1 (or_1_out, and_2_out, and_3_out);
  or or_2 (or_2_out, or_1_out, and_4_out);

  // Notes on the sheet:
  //   D1
  //   D0
endmodule

module Ejercicio_3 (
  input  in_1,
  input  [7:0] in_2,
  output [7:0] out_3
);

  wire not_1_out, not_2_out, not_3_out, not_4_out, not_5_out, not_6_out, not_7_out, not_8_out;

  not not_1 (not_1_out, in_2[0]);
  not not_2 (not_2_out, in_2[1]);
  not not_3 (not_3_out, in_2[4]);
  not not_4 (not_4_out, in_2[6]);
  not not_5 (not_5_out, in_2[7]);
  not not_6 (not_6_out, in_2[2]);
  not not_7 (not_7_out, in_2[3]);
  not not_8 (not_8_out, in_2[5]);
  S_R_Flip_Flop s_r_ff_1 (.S(in_2[0]), .clk(in_1), .R(not_1_out), .Q(out_3[0]));  // open: Qn, preset, reset, en
  S_R_Flip_Flop s_r_ff_2 (.S(in_2[1]), .clk(in_1), .R(not_2_out), .Q(out_3[1]));  // open: Qn, preset, reset, en
  S_R_Flip_Flop s_r_ff_3 (.S(in_2[2]), .clk(in_1), .R(not_6_out), .Q(out_3[2]));  // open: Qn, preset, reset, en
  S_R_Flip_Flop s_r_ff_4 (.S(in_2[3]), .clk(in_1), .R(not_7_out), .Q(out_3[3]));  // open: Qn, preset, reset, en
  S_R_Flip_Flop s_r_ff_5 (.S(in_2[4]), .clk(in_1), .R(not_3_out), .Q(out_3[4]));  // open: Qn, preset, reset, en
  S_R_Flip_Flop s_r_ff_6 (.S(in_2[5]), .clk(in_1), .R(not_8_out), .Q(out_3[5]));  // open: Qn, preset, reset, en
  S_R_Flip_Flop s_r_ff_7 (.S(in_2[6]), .clk(in_1), .R(not_4_out), .Q(out_3[6]));  // open: Qn, preset, reset, en
  S_R_Flip_Flop s_r_ff_8 (.S(in_2[7]), .clk(in_1), .R(not_5_out), .Q(out_3[7]));  // open: Qn, preset, reset, en
endmodule

module Ejercicio_4 (
  input  [1:0] in_1,
  input  [1:0] in_2,
  input  [7:0] in_3,
  input  [1:0] in_4,
  input  in_5,
  output [7:0] out_6,
  output [7:0] out_7
);

  wire and_1_out, and_2_out, and_3_out, and_4_out;
  wire [7:0] demultiplexer_1_out0, demultiplexer_1_out1, demultiplexer_1_out2, demultiplexer_1_out3,
       ejercicio_3_1_out_3, ejercicio_3_2_out_3, ejercicio_3_3_out_3, ejercicio_3_4_out_3;

  Demultiplexer #(.select(2), .width(8)) demultiplexer_1 (
    .out0(demultiplexer_1_out0), .out1(demultiplexer_1_out1), .out2(demultiplexer_1_out2),
    .out3(demultiplexer_1_out3), .in(in_3), .sel(in_4));  // open: en
  and and_1 (and_1_out, ~in_4[0], ~in_4[1], in_5);  // AND_Gate
  and and_2 (and_2_out, in_4[0], ~in_4[1], in_5);  // AND_Gate
  and and_3 (and_3_out, in_4[0], in_4[1], in_5);
  and and_4 (and_4_out, ~in_4[0], in_4[1], in_5);  // AND_Gate
  Ejercicio_3 ejercicio_3_1 (.in_1(and_1_out), .in_2(demultiplexer_1_out0), .out_3(ejercicio_3_1_out_3));
  Ejercicio_3 ejercicio_3_2 (.in_1(and_2_out), .in_2(demultiplexer_1_out1), .out_3(ejercicio_3_2_out_3));
  Ejercicio_3 ejercicio_3_3 (.in_1(and_4_out), .in_2(demultiplexer_1_out2), .out_3(ejercicio_3_3_out_3));
  Ejercicio_3 ejercicio_3_4 (.in_1(and_3_out), .in_2(demultiplexer_1_out3), .out_3(ejercicio_3_4_out_3));
  Multiplexer #(.select(2), .width(8), .enable("false")) multiplexer_1 (
    .in0(ejercicio_3_1_out_3), .in1(ejercicio_3_2_out_3), .in2(ejercicio_3_3_out_3),
    .in3(ejercicio_3_4_out_3), .out(out_6), .sel(in_1));
  Multiplexer #(.select(2), .width(8), .enable("false")) multiplexer_2 (
    .in0(ejercicio_3_1_out_3), .in1(ejercicio_3_2_out_3), .in2(ejercicio_3_3_out_3),
    .in3(ejercicio_3_4_out_3), .out(out_7), .sel(in_2));
endmodule
